// Logisim project lab3.circ as structural Verilog: 1 circuit, main circuit main
module main (
  input  in_1,
  input  in_2,
  input  in_3,
  input  in_4,
  input  in_5,
  input  in_6,
  output out_7
);

  wire and_1_out, and_2_out, and_3_out, multiplexer_1_out, undriven_2;
  wire [2:0] undriven;

  Multiplexer #(.select(3)) multiplexer_1 (
    .in0(1'b0), .in1(1'b0), .in2(1'b0), .in3(1'b1), .in4(1'b0), .in5(1'b1), .in6(1'b1), .in7(1'b1),
    .out(multiplexer_1_out), .sel(undriven), .en(undriven_2));
  and and_1 (and_1_out, in_3, in_1);
  and and_2 (and_2_out, in_1, in_2);
  and and_3 (and_3_out, in_2, in_3);
  or or_1 (out_7, and_1_out, and_2_out, and_3_out);

  // Notes on the sheet:
  //   Majority Circut
endmodule
