// Logisim project lab4.circ as structural Verilog: 1 circuit, main circuit main
module main (
  input  Goat,
  input  Wolf,
  input  Cabbage,
  output out_4
);

  wire clock_1_out, d_ff_1_q, d_ff_2_q, d_ff_3_q, not_1_out, t_ff_1_q;

  Clock clock_1 (.out(clock_1_out));
  D_Flip_Flop d_ff_1 (.clk(clock_1_out), .D(Goat), .Q(d_ff_1_q));  // open: Qn, preset, en, reset
  D_Flip_Flop d_ff_2 (.clk(clock_1_out), .D(Wolf), .Q(d_ff_2_q));  // open: Qn, preset, en, reset
  D_Flip_Flop d_ff_3 (.clk(clock_1_out), .D(Cabbage), .Q(d_ff_3_q));  // open: Qn, preset, en, reset
  T_Flip_Flop t_ff_1 (.clk(clock_1_out), .T(1'b1), .Q(t_ff_1_q));  // open: Qn, preset, reset, en
  not not_1 (not_1_out, t_ff_1_q);
  and and_1 (out_4, d_ff_1_q, d_ff_2_q, d_ff_3_q, not_1_out);

  // Notes on the sheet:
  //   Farmer
endmodule
