// Logisim project register.circ as structural Verilog: 2 circuits, main circuit main
module main (
  input  [15:0] in_1,
  input  Clock,
  input  [1:0] Ra,
  input  [1:0] Rd,
  input  [1:0] Rb,
  output [15:0] out_6,
  output [15:0] out_7
);

  wire demultiplexer_1_out0, demultiplexer_1_out1, demultiplexer_1_out2, demultiplexer_1_out3;
  wire [15:0] register_1_q, register_2_q, register_3_q, register_4_q;

  Demultiplexer #(.select(2)) demultiplexer_1 (
    .out0(demultiplexer_1_out0), .out1(demultiplexer_1_out1), .out2(demultiplexer_1_out2),
    .out3(demultiplexer_1_out3), .in(Clock), .sel(Rd));  // open: en
  Register #(.width(16)) register_1 (.D(in_1), .Q(register_1_q), .clk(demultiplexer_1_out0));  // open: en, clr
  Register #(.width(16)) register_2 (.D(in_1), .Q(register_2_q), .clk(demultiplexer_1_out1));  // open: en, clr
  Register #(.width(16)) register_3 (.D(in_1), .Q(register_3_q), .clk(demultiplexer_1_out2));  // open: en, clr
  Register #(.width(16)) register_4 (.D(in_1), .Q(register_4_q), .clk(demultiplexer_1_out3));  // open: en, clr
  Multiplexer #(.select(2), .width(16)) multiplexer_1 (
    .in0(register_1_q), .in1(register_2_q), .in2(register_3_q), .in3(register_4_q), .out(out_6), .sel(Ra));  // open: en
  Multiplexer #(.select(2), .width(16)) multiplexer_2 (
    .in0(register_1_q), .in1(register_2_q), .in2(register_3_q), .in3(register_4_q), .out(out_7), .sel(Rb));  // open: en
endmodule

module test (
  input  [15:0] in_1,
  input  [3:0] in_2
);

  wire clock_1_out, demultiplexer_1_out0, demultiplexer_1_out1, demultiplexer_1_out2, demultiplexer_1_out3;

  Clock clock_1 (.out(clock_1_out));
  Demultiplexer #(.select(2)) demultiplexer_1 (
    .out0(demultiplexer_1_out0), .out1(demultiplexer_1_out1), .out2(demultiplexer_1_out2),
    .out3(demultiplexer_1_out3), .in(clock_1_out), .sel(in_2[1:0]));  // open: en
  main main_1 (.in_1(in_1), .Clock(demultiplexer_1_out0), .Rd(in_2[3:2]));  // open: Ra, Rb, out_6, out_7
  main main_2 (.in_1(in_1), .Clock(demultiplexer_1_out1), .Rd(in_2[3:2]));  // open: Ra, Rb, out_6, out_7
  main main_3 (.in_1(in_1), .Clock(demultiplexer_1_out2), .Rd(in_2[3:2]));  // open: Ra, Rb, out_6, out_7
  main main_4 (.in_1(in_1), .Clock(demultiplexer_1_out3), .Rd(in_2[3:2]));  // open: Ra, Rb, out_6, out_7
endmodule
